// Logisim project demoV1.circ as structural Verilog: 18 circuits, main circuit IF
module IF (
  input  clk,
  input  rest,
  input  stallStageIF,
  input  [31:0] branchTarget_ID,
  input  branchFlag_ID,
  output [31:0] PC_IF,
  output [31:0] instr_IF
);

  wire stallStageIF_t;
  wire [31:0] adder_1_out, nextPC;

  not not_1 (stallStageIF_t, stallStageIF);
  Adder #(.width(32)) adder_1 (.a(PC_IF), .b(32'h4), .out(adder_1_out));  // open: cin, cout
  Register #(.width(32)) PC (.D(nextPC), .en(stallStageIF_t), .Q(PC_IF), .clk(clk), .clr(rest));
  Multiplexer #(.width(32), .disabled(0), .enable("false")) multiplexer_1 (
    .in0(adder_1_out), .in1(branchTarget_ID), .out(nextPC), .sel(branchFlag_ID));
  ROM #(.addrWidth(6), .dataWidth(32)) rom_1 (.addr(PC_IF[7:2]), .data(instr_IF));  // open: sel

  // Other names for the same wires on the sheet: branchFlag = branchFlag_ID; branchTarget[31:0] = branchTarget_ID

  // Notes on the sheet:
  //   指令存储器
  //   contents of rom_1 (hex, n*v repeats v):
  //   2800401 2800802 2800c03 2801004 4c001885 2801405 2801806 2801c07 2802008
endmodule

module IF_ID (
  input  clk,
  input  reset,
  input  flushStageID,
  input  stallStageID,
  input  [31:0] PC_IF,
  input  [31:0] instr_IF,
  output [31:0] PC_ID,
  output [31:0] instr_ID
);

  wire stall;

  not not_1 (stall, stallStageID);
  Reg32 PC (.D(PC_IF), .EN(stall), .flush(flushStageID), .clk(clk), .rest(reset), .Q(PC_ID));
  Reg32 instr (.D(instr_IF), .EN(stall), .flush(flushStageID), .clk(clk), .rest(reset), .Q(instr_ID));

  // Other names for the same wires on the sheet: flush = flushStageID
endmodule

module ID (
  input  clk,
  input  rst,
  input  [31:0] PC_ID,
  input  [31:0] instr_ID,
  input  [4:0] wRegAddr_WB,
  input  [31:0] wRegData_WB,
  input  weReg_ctrl_WB,
  input  [4:0] wRegAddr_EXE,
  input  [4:0] wRegAddr_MEM,
  input  [31:0] aluResult_EXE,
  input  wRegDataSrc_ctrl_uMEM_EXE,
  input  [31:0] wRegData_MEM,
  output [31:0] data1_ID,
  output [31:0] data2_ID,
  output [4:0] wRegAddr_ID,
  output [31:0] wMemData_ID,
  output [31:0] branchTarget_ID,
  output branchFlag_ID,
  output stallReqOfID_ID,
  output flushReqOfID_ID,
  output weReg_ctrl_uWB_ID,
  output memReadDataExt_ctrl_uMEM_ID,
  output [1:0] wrMemByteSelScr_ctrl_uMEM_ID,
  output wRegDataSrc_ctrl_uMEM_ID,
  output weMEM_ctrl_uMEM_ID,
  output [3:0] aluOP_ctrl_uEXE_ID
);

  wire ADD, ADDI, and_1_out, and_2_out, and_3_out, and_5_out, and_6_out, and_7_out, and_9_out, and_10_out,
       and_11_out, and_12_out, and_13_out, BEQ, BEQ_result, BGE, BGE_result, BL, BLTU, BLTU_result,
       comparator_12_eq, comparator_13_eq, comparator_14_eq, comparator_15_eq, comparator_16_eq,
       comparator_17_eq, comparator_23_eq, comparator_24_eq, comparator_25_eq, comparator_26_eq,
       comparator_27_eq, comparator_28_eq, JIRL, LDB, LDH, LDW, LU12I, not_1_out, not_2_out, not_3_out,
       not_4_out, not_5_out, not_6_out, not_7_out, not_8_out, raddr1Src_ctrl_uID, stall_case1, stall_case2,
       STB, stFlag, STH, STW;
  wire [1:0] data1Src_ctrl_uID, data2Src_ctrl_uID, immSrc_ctrl_uID, priority_encoder_1_out,
       priority_encoder_2_out, raddr2Src_ctrl_uID, wMemDataMaskSrc_ctrl_uID;
  wire [1:1] wRegAddrSrc_ctrl_uID;
  wire [4:0] raddr_1, raddr_2;
  wire [31:0] bit_extender_2_out, bit_extender_3_out, bit_extender_4_out, ext_o16, ext_o26, ext_si12,
       ext_si20, imm, multiplexer_6_out, multiplexer_8_out, reg_raw_rdata1, reg_raw_rdata2, regReadData1,
       regReadData2;

  // Probe on raddr_1
  assign ext_si12 = {{20{instr_ID[21]}}, instr_ID[21:10]};  // Bit_Extender bit_extender_1
  assign bit_extender_2_out = {{12{instr_ID[24]}}, instr_ID[24:5]};  // Bit_Extender bit_extender_2
  assign bit_extender_3_out = {{16{instr_ID[25]}}, instr_ID[25:10]};  // Bit_Extender bit_extender_3
  assign bit_extender_4_out = {{6{instr_ID[9]}}, {instr_ID[9:0], instr_ID[25:10]}};  // Bit_Extender bit_extender_4
  RegFiles RegFile (
    .clk(clk), .rest(rst), .raddr1_ID(raddr_1), .raddr2_ID(raddr_2), .wr_data_WB(wRegData_WB),
    .wr_addr_WB(wRegAddr_WB), .wr_en_ctrl_WB(weReg_ctrl_WB), .rdata1(reg_raw_rdata1), .rdata2(reg_raw_rdata2));
  Multiplexer #(.width(5), .disabled(0), .enable("false")) multiplexer_1 (
    .in0({5{1'b0}}), .in1(instr_ID[9:5]), .out(raddr_1), .sel(raddr1Src_ctrl_uID));
  Multiplexer #(.select(2), .width(5), .disabled(0), .enable("false")) multiplexer_2 (
    .in0({5{1'b0}}), .in1(instr_ID[14:10]), .in2(instr_ID[4:0]), .out(raddr_2), .sel(raddr2Src_ctrl_uID));  // open: in3
  // Probe on raddr_2
  Shifter #(.width(32)) shifter_1 (.in(bit_extender_2_out), .\dist (5'b01100), .out(ext_si20));
  Shifter #(.width(32)) shifter_2 (.in(bit_extender_3_out), .\dist (5'b00010), .out(ext_o16));
  Shifter #(.width(32)) shifter_3 (.in(bit_extender_4_out), .\dist (5'b00010), .out(ext_o26));
  Comparator #(.width(10), .mode("unsigned")) comparator_1 (.a(instr_ID[31:22]), .b(10'ha), .eq(ADDI));  // open: gt, lt
  Comparator #(.width(10), .mode("unsigned")) comparator_2 (.a(instr_ID[31:22]), .b(10'ha0), .eq(LDB));  // open: gt, lt
  Comparator #(.width(10), .mode("unsigned")) comparator_3 (.a(instr_ID[31:22]), .b(10'ha1), .eq(LDH));  // open: gt, lt
  Comparator #(.width(10), .mode("unsigned")) comparator_4 (.a(instr_ID[31:22]), .b(10'ha2), .eq(LDW));  // open: gt, lt
  Comparator #(.width(10), .mode("unsigned")) comparator_5 (.a(instr_ID[31:22]), .b(10'ha4), .eq(STB));  // open: gt, lt
  Comparator #(.width(10), .mode("unsigned")) comparator_6 (.a(instr_ID[31:22]), .b(10'ha5), .eq(STH));  // open: gt, lt
  Comparator #(.width(10), .mode("unsigned")) comparator_7 (.a(instr_ID[31:22]), .b(10'ha6), .eq(STW));  // open: gt, lt
  Comparator #(.width(6), .mode("unsigned")) comparator_8 (
    .a(instr_ID[31:26]), .b(6'b010011), .eq(JIRL));  // open: gt, lt
  Comparator #(.width(6), .mode("unsigned")) comparator_9 (
    .a(instr_ID[31:26]), .b(6'b010110), .eq(BEQ));  // open: gt, lt
  Comparator #(.width(6), .mode("unsigned")) comparator_10 (
    .a(instr_ID[31:26]), .b(6'b011001), .eq(BGE));  // open: gt, lt
  Comparator #(.width(6), .mode("unsigned")) comparator_11 (
    .a(instr_ID[31:26]), .b(6'b011010), .eq(BLTU));  // open: gt, lt
  Multiplexer #(.select(3), .width(32), .disabled(0), .enable("false")) multiplexer_3 (
    .in0({32{1'b0}}), .in1(ext_si12), .in2(ext_si20), .in3(ext_o16), .in4(ext_o26), .in5({32{1'b0}}),
    .in6({32{1'b0}}), .in7({32{1'b0}}), .out(imm), .sel({BL, immSrc_ctrl_uID}));
  // Probe on imm
  not not_1 (not_1_out, comparator_12_eq);
  Comparator #(.width(5), .mode("unsigned")) comparator_12 (
    .a(wRegAddr_EXE), .b({5{1'b0}}), .eq(comparator_12_eq));  // open: gt, lt
  Comparator #(.width(5), .mode("unsigned")) comparator_13 (
    .a(wRegAddr_EXE), .b(raddr_1), .eq(comparator_13_eq));  // open: gt, lt
  not not_2 (not_2_out, wRegDataSrc_ctrl_uMEM_EXE);
  Comparator #(.width(5), .mode("unsigned")) comparator_14 (
    .a(wRegAddr_MEM), .b({5{1'b0}}), .eq(comparator_14_eq));  // open: gt, lt
  not not_3 (not_3_out, comparator_14_eq);
  Comparator #(.width(5), .mode("unsigned")) comparator_15 (
    .a(wRegAddr_MEM), .b(raddr_1), .eq(comparator_15_eq));  // open: gt, lt
  Comparator #(.width(5), .mode("unsigned")) comparator_16 (
    .a(wRegAddr_WB), .b({5{1'b0}}), .eq(comparator_16_eq));  // open: gt, lt
  not not_4 (not_4_out, comparator_16_eq);
  Comparator #(.width(5), .mode("unsigned")) comparator_17 (
    .a(wRegAddr_WB), .b(raddr_1), .eq(comparator_17_eq));  // open: gt, lt
  and and_1 (and_1_out, not_3_out, comparator_15_eq);
  and and_2 (and_2_out, not_1_out, comparator_13_eq, not_2_out);
  Comparator #(.width(7), .mode("unsigned")) comparator_18 (
    .a(instr_ID[31:25]), .b(7'b0001010), .eq(LU12I));  // open: gt, lt
  Comparator #(.width(6), .mode("unsigned")) comparator_19 (
    .a(instr_ID[31:26]), .b(6'b010101), .eq(BL));  // open: gt, lt
  and and_3 (and_3_out, not_4_out, comparator_17_eq);
  and and_4 (stall_case1, not_1_out, comparator_13_eq, wRegDataSrc_ctrl_uMEM_EXE);
  Priority_Encoder #(.select(2)) priority_encoder_1 (
    .in0(1'b1), .in1(and_3_out), .in2(and_1_out), .in3(and_2_out), .out(priority_encoder_1_out));  // open: gs, en_out, en_in
  Multiplexer #(.select(2), .width(32), .disabled(0), .enable("false")) multiplexer_4 (
    .in0(reg_raw_rdata1), .in1(reg_raw_rdata1), .in2(wRegData_MEM), .in3(aluResult_EXE), .out(regReadData1),
    .sel(priority_encoder_1_out));
  Comparator #(.width(17), .mode("unsigned")) comparator_20 (
    .a(instr_ID[31:15]), .b(17'h20), .eq(ADD));  // open: gt, lt
  Comparator #(.width(17), .mode("unsigned")) comparator_21 (
    .a(instr_ID[31:15]), .b(17'h2f), .eq(aluOP_ctrl_uEXE_ID[2]));  // open: gt, lt
  Comparator #(.width(17), .mode("unsigned")) comparator_22 (
    .a(instr_ID[31:15]), .b(17'h30), .eq(aluOP_ctrl_uEXE_ID[3]));  // open: gt, lt
  or or_1 (stFlag, STB, STH, STW);
  Comparator #(.width(5), .mode("unsigned")) comparator_23 (
    .a(wRegAddr_EXE), .b({5{1'b0}}), .eq(comparator_23_eq));  // open: gt, lt
  Comparator #(.width(5), .mode("unsigned")) comparator_24 (
    .a(wRegAddr_EXE), .b(raddr_2), .eq(comparator_24_eq));  // open: gt, lt
  Comparator #(.width(5), .mode("unsigned")) comparator_25 (
    .a(wRegAddr_MEM), .b({5{1'b0}}), .eq(comparator_25_eq));  // open: gt, lt
  Comparator #(.width(5), .mode("unsigned")) comparator_26 (
    .a(wRegAddr_MEM), .b(raddr_2), .eq(comparator_26_eq));  // open: gt, lt
  Comparator #(.width(5), .mode("unsigned")) comparator_27 (
    .a(wRegAddr_WB), .b({5{1'b0}}), .eq(comparator_27_eq));  // open: gt, lt
  Comparator #(.width(5), .mode("unsigned")) comparator_28 (
    .a(wRegAddr_WB), .b(raddr_2), .eq(comparator_28_eq));  // open: gt, lt
  or or_2 (weReg_ctrl_uWB_ID, ADD, aluOP_ctrl_uEXE_ID[2], aluOP_ctrl_uEXE_ID[3], ADDI, LDB, LDH, LDW, LU12I, BL, JIRL);
  not not_5 (not_5_out, comparator_23_eq);
  not not_6 (not_6_out, wRegDataSrc_ctrl_uMEM_EXE);
  not not_7 (not_7_out, comparator_25_eq);
  not not_8 (not_8_out, comparator_27_eq);
  and and_5 (and_5_out, not_5_out, comparator_24_eq, not_6_out);
  and and_6 (and_6_out, not_7_out, comparator_26_eq);
  and and_7 (and_7_out, not_8_out, comparator_28_eq);
  and and_8 (stall_case2, not_5_out, comparator_24_eq, wRegDataSrc_ctrl_uMEM_EXE);
  Comparator #(.width(32), .mode("unsigned")) comparator_29 (
    .a(regReadData1), .b(regReadData2), .eq(BEQ_result), .lt(BLTU_result));  // open: gt
  Comparator #(.width(32)) comparator_30 (.a(regReadData1), .b(regReadData2), .gt(BGE_result));  // open: eq, lt
  Priority_Encoder #(.select(2)) priority_encoder_2 (
    .in0(1'b1), .in1(and_7_out), .in2(and_6_out), .in3(and_5_out), .out(priority_encoder_2_out));  // open: gs, en_out, en_in
  Multiplexer #(.select(2), .width(32), .disabled(0), .enable("false")) multiplexer_5 (
    .in0(reg_raw_rdata2), .in1(reg_raw_rdata2), .in2(wRegData_MEM), .in3(aluResult_EXE), .out(regReadData2),
    .sel(priority_encoder_2_out));
  or or_3 (memReadDataExt_ctrl_uMEM_ID, LDB, LDH, LDW);
  // Probe on regReadData1
  // Probe on branchTarget_ID
  or or_4 (wrMemByteSelScr_ctrl_uMEM_ID[1], LDH, LDW, STH, STW);
  Multiplexer #(.width(32), .disabled(0), .enable("false")) multiplexer_6 (
    .in0(PC_ID), .in1(regReadData1), .out(multiplexer_6_out), .sel(JIRL));
  or or_5 (wrMemByteSelScr_ctrl_uMEM_ID[0], LDB, LDW, STB, STW);
  Multiplexer #(.select(2), .width(5), .disabled(0), .enable("false")) multiplexer_7 (
    .in0({5{1'b0}}), .in1(5'b00001), .in2(instr_ID[4:0]), .in3({5{1'b0}}), .out(wRegAddr_ID),
    .sel({wRegAddrSrc_ctrl_uID[1], BL}));
  Multiplexer #(.select(2), .width(32), .disabled(0), .enable("false")) multiplexer_8 (
    .in0({32{1'b0}}), .in1(32'hff), .in2(32'hffff), .in3({32{1'b1}}), .out(multiplexer_8_out),
    .sel(wMemDataMaskSrc_ctrl_uID));
  // Probe on wMemDataMaskSrc_ctrl_uID
  and and_9 (and_9_out, BEQ, BEQ_result);
  and and_10 (and_10_out, BLTU, BLTU_result);
  and and_11 (and_11_out, BGE, BGE_result);
  and and_12 (and_12_out, JIRL, 1'b1);
  and and_13 (and_13_out, BL, 1'b1);
  Adder #(.width(32)) adder_1 (.a(multiplexer_6_out), .b(imm), .out(branchTarget_ID));  // open: cin, cout
  Multiplexer #(.select(2), .width(32), .disabled(0), .enable("false")) multiplexer_9 (
    .in0({32{1'b0}}), .in1(regReadData1), .in2(PC_ID), .in3({32{1'b0}}), .out(data1_ID),
    .sel(data1Src_ctrl_uID));
  Multiplexer #(.select(2), .width(32), .disabled(0), .enable("false")) multiplexer_10 (
    .in0({32{1'b0}}), .in1(regReadData2), .in2(imm), .in3(32'h4), .out(data2_ID), .sel(data2Src_ctrl_uID));
  // Probe on wMemData_ID
  or or_6 (branchFlag_ID, and_9_out, and_10_out, and_11_out, and_12_out, and_13_out);
  assign wMemData_ID = regReadData2 & multiplexer_8_out;  // AND_Gate and_14, 32 bits wide
  or or_7 (wRegDataSrc_ctrl_uMEM_ID, LDB, LDH, LDW);
  or or_8 (stallReqOfID_ID, stall_case1, stall_case2);
  or or_9 (weMEM_ctrl_uMEM_ID, STB, STH, STW);
  or or_10 (aluOP_ctrl_uEXE_ID[1], ADD, ADDI, LDB, LDH, LDW, STB, STH, STW, BL, JIRL);
  or or_11 (aluOP_ctrl_uEXE_ID[0], LU12I, BEQ, BGE, BLTU);
  or or_12 (immSrc_ctrl_uID[1], LU12I, JIRL, BEQ, BGE, BLTU);
  or or_13 (immSrc_ctrl_uID[0], ADDI, LDB, LDH, LDW, STB, STH, STW, JIRL, BEQ, BGE, BLTU);
  // Probe on {BL, immSrc_ctrl_uID}
  or or_14 (wMemDataMaskSrc_ctrl_uID[0], STB, STW);
  or or_15 (wMemDataMaskSrc_ctrl_uID[1], STH, STW);
  // Probe on wMemDataMaskSrc_ctrl_uID
  or or_16 (wRegAddrSrc_ctrl_uID[1], ADD, aluOP_ctrl_uEXE_ID[2], aluOP_ctrl_uEXE_ID[3], ADDI, LDB, LDH, LDW, LU12I, JIRL);
  // Probe on {wRegAddrSrc_ctrl_uID[1], BL}
  or or_17 (raddr2Src_ctrl_uID[1], STB, STH, STW, BEQ, BGE, BLTU);
  or or_18 (raddr2Src_ctrl_uID[0], ADD, aluOP_ctrl_uEXE_ID[2], aluOP_ctrl_uEXE_ID[3]);
  // Probe on raddr2Src_ctrl_uID
  or or_19 (data2Src_ctrl_uID[1], ADDI, LDB, LDH, LDW, STB, STH, STW, LU12I, BL, JIRL);
  or or_20 (data2Src_ctrl_uID[0], ADD, aluOP_ctrl_uEXE_ID[2], aluOP_ctrl_uEXE_ID[3], BL, JIRL);
  // Probe on data2Src_ctrl_uID
  or or_21 (raddr1Src_ctrl_uID, ADD, aluOP_ctrl_uEXE_ID[2], aluOP_ctrl_uEXE_ID[3], ADDI, LDB, LDH, LDW, STB, STH, STW, JIRL, BEQ, BGE, BLTU);
  // Probe on raddr1Src_ctrl_uID
  or or_22 (data1Src_ctrl_uID[1], BL, JIRL);
  or or_23 (data1Src_ctrl_uID[0], ADD, aluOP_ctrl_uEXE_ID[2], aluOP_ctrl_uEXE_ID[3], ADDI, LDB, LDH, LDW, STB, STH, STW);
  // Probe on data1Src_ctrl_uID

  assign flushReqOfID_ID = branchFlag_ID;

  // Other names for the same wires on the sheet: aluOP_ctrl_uEXE[3:0] = aluOP_ctrl_uEXE_ID;
  //   SRL = aluOP_ctrl_uEXE_ID[2]; SRA = aluOP_ctrl_uEXE_ID[3]; branchTarget[31:0] = branchTarget_ID;
  //   data1[31:0] = data1_ID; data2[31:0] = data2_ID; branchFlag = branchFlag_ID; flushReq = branchFlag_ID;
  //   i16[15:0] = instr_ID[25:10]; i21[20:0] = {instr_ID[4:0], instr_ID[25:10]};
  //   i26[25:0] = {instr_ID[9:0], instr_ID[25:10]}; instr[31:0] = instr_ID; o16[15:0] = instr_ID[25:10];
  //   o26[25:0] = {instr_ID[9:0], instr_ID[25:10]}; rk[4:0] = instr_ID[14:10]; si12[11:0] = instr_ID[21:10];
  //   si20[19:0] = instr_ID[24:5]; ui12[11:0] = instr_ID[21:10]; op_3R[16:0] = instr_ID[31:15];
  //   op_2RI12[9:0] = instr_ID[31:22]; op_1RI20[6:0] = instr_ID[31:25]; rd[4:0] = instr_ID[4:0];
  //   op_1RI21[5:0] = instr_ID[31:26]; op_2RI16[5:0] = instr_ID[31:26]; op_I26[5:0] = instr_ID[31:26];
  //   ldFlag_EXE = wRegDataSrc_ctrl_uMEM_EXE; memReadDataExt_ctrl_uMEM = memReadDataExt_ctrl_uMEM_ID;
  //   rj[4:0] = instr_ID[9:5]; PC[31:0] = PC_ID; stallReq = stallReqOfID_ID; weMEM_ctrl_uMEM = weMEM_ctrl_uMEM_ID;
  //   weReg_ctrl_uWB = weReg_ctrl_uWB_ID; wMemData[31:0] = wMemData_ID; wRegAddr[4:0] = wRegAddr_ID;
  //   immSrc_ctrl_uID[2] = BL; wRegAddrSrc_ctrl_uID[0] = BL; wRegDataSrc_ctrl_uMEM = wRegDataSrc_ctrl_uMEM_ID;
  //   wrMemByteSelScr_ctrl_uMEM[1:0] = wrMemByteSelScr_ctrl_uMEM_ID

  // Notes on the sheet:
  //   ADD
  //   raddr1 接rj
  //   raddr2接rk
  //   waddr接rd
  //   主要用于相关检测的输入接口
  //   字段提取
  //   寄存器堆
  //   译码
  //   相关处理
  //   分支处理
endmodule

module EXE (
  input  [3:0] aluOP_ctrl_uEXE_EXE,
  input  [31:0] data1_EXE,
  input  [31:0] data2_EXE,
  output [31:0] aluResult_EXE
);

  ALU ALU (.aluop(aluOP_ctrl_uEXE_EXE), .A(data1_EXE), .B(data2_EXE), .aluResult(aluResult_EXE));
endmodule

module EXE_MEM (
  input  clk,
  input  reset,
  input  flushStageMEM,
  input  stallStageMEM,
  input  [31:0] aluResult_EXE,
  input  [4:0] wRegAddr_EXE,
  input  [31:0] wMemData_EXE,
  input  weMem_ctrl_uMEM_EXE,
  input  wRegDataSrc_ctrl_uMEM_EXE,
  input  [1:0] wrMemByteSelScr_ctrl_uMEM_EXE,
  input  memReadDataExt_ctrl_uMEM_EXE,
  input  weReg_ctrl_uWB_EXE,
  output [31:0] aluResult_MEM,
  output [4:0] wRegAddr_MEM,
  output [31:0] wMemData_MEM,
  output weMem_ctrl_uMEM_MEM,
  output wRegDataSrc_ctrl_uMEM_MEM,
  output [1:0] wrMemByteSelScr_ctrl_uMEM_MEM,
  output memReadDataExt_ctrl_uMEM_MEM,
  output weReg_ctrl_uWB_MEM
);

  wire stall;

  not not_1 (stall, stallStageMEM);
  Reg32 aluResult (.D(aluResult_EXE), .EN(stall), .flush(flushStageMEM), .clk(clk), .rest(reset), .Q(aluResult_MEM));
  Reg5 wRegAddr (.D(wRegAddr_EXE), .EN(stall), .flush(flushStageMEM), .clk(clk), .rest(reset), .Q(wRegAddr_MEM));
  Reg32 wMemData (.D(wMemData_EXE), .EN(stall), .flush(flushStageMEM), .clk(clk), .rest(reset), .Q(wMemData_MEM));
  Reg1 weMEM_ctrl_uMEM (
    .D(weMem_ctrl_uMEM_EXE), .EN(stall), .flush(flushStageMEM), .clk(clk), .rest(reset),
    .Q(weMem_ctrl_uMEM_MEM));
  Reg1 wRegDataSrc_ctrl_uMEM (
    .D(wRegDataSrc_ctrl_uMEM_EXE), .EN(stall), .flush(flushStageMEM), .clk(clk), .rest(reset),
    .Q(wRegDataSrc_ctrl_uMEM_MEM));
  Reg2 wrMemByteSelScr_ctrl_uMEM (
    .D(wrMemByteSelScr_ctrl_uMEM_EXE), .EN(stall), .flush(flushStageMEM), .clk(clk), .rest(reset),
    .Q(wrMemByteSelScr_ctrl_uMEM_MEM));
  Reg1 wrMemByteSelScr_ctrl_uMEM_2 (
    .D(memReadDataExt_ctrl_uMEM_EXE), .EN(stall), .flush(flushStageMEM), .clk(clk), .rest(reset),
    .Q(memReadDataExt_ctrl_uMEM_MEM));
  Reg1 weReg_ctrl_uWB (
    .D(weReg_ctrl_uWB_EXE), .EN(stall), .flush(flushStageMEM), .clk(clk), .rest(reset), .Q(weReg_ctrl_uWB_MEM));

  // Other names for the same wires on the sheet: flush = flushStageMEM
endmodule

module MEM (
  input  clk,
  input  reset,
  input  [31:0] aluResult_MEM,
  input  [31:0] wMemData_MEM,
  input  weMEM_ctrl_uMEM_MEM,
  input  wRegDataSrc_ctrl_uMEM_MEM,
  input  [1:0] wrMemByteSelScr_ctrl_uMEM_MEM,
  input  memReadDataExt_ctrl_uMEM_MEM,
  output [31:0] wRegData_MEM
);

  wire not_1_out;
  wire [3:0] byteSel, decoder_1_out0, multiplexer_1_out;
  wire [7:0] multiplexer_4_out, rdata0, rdata1, rdata2, rdata3, wdata0, wdata1, wdata2, wdata3;
  wire [15:0] multiplexer_5_out;
  wire [31:0] bit_extender_1_out, bit_extender_2_out, bit_extender_3_out, bit_extender_4_out, readByteData,
       readHalfWordData, readMemData;

  not not_1 (not_1_out, weMEM_ctrl_uMEM_MEM);
  // Probe on rdata0
  RAM #(.addrWidth(6), .bus("separate")) ram_1 (
    .addr(aluResult_MEM[7:2]), .din(wdata0), .data(rdata0), .str(weMEM_ctrl_uMEM_MEM), .sel(byteSel[0]),
    .clk(clk), .ld(not_1_out), .clr(reset));
  Decoder #(.select(2), .disabled(0), .enable("false")) decoder_1 (
    .out0(decoder_1_out0[0]), .out1(decoder_1_out0[1]), .out2(decoder_1_out0[2]), .out3(decoder_1_out0[3]),
    .sel(aluResult_MEM[1:0]));
  Multiplexer #(.width(4), .disabled(0), .enable("false")) multiplexer_1 (
    .in0(4'b0011), .in1(4'b1100), .out(multiplexer_1_out), .sel(aluResult_MEM[1]));
  // Probe on rdata1
  RAM #(.addrWidth(6), .bus("separate")) ram_2 (
    .addr(aluResult_MEM[7:2]), .din(wdata1), .data(rdata1), .str(weMEM_ctrl_uMEM_MEM), .sel(byteSel[1]),
    .clk(clk), .ld(not_1_out), .clr(reset));
  Multiplexer #(.select(2), .width(4), .disabled(0), .enable("false")) multiplexer_2 (
    .in0(4'b0000), .in1(decoder_1_out0), .in2(multiplexer_1_out), .in3(4'b1111), .out(byteSel),
    .sel(wrMemByteSelScr_ctrl_uMEM_MEM));
  Multiplexer #(.select(2), .width(32), .disabled(0), .enable("false")) multiplexer_3 (
    .in0({32{1'b0}}), .in1({wMemData_MEM[7:0], wMemData_MEM[7:0], wMemData_MEM[7:0], wMemData_MEM[7:0]}),
    .in2({wMemData_MEM[15:0], wMemData_MEM[15:0]}), .in3(wMemData_MEM),
    .out({wdata3, wdata2, wdata1, wdata0}), .sel(wrMemByteSelScr_ctrl_uMEM_MEM));
  // Probe on rdata2
  RAM #(.addrWidth(6), .bus("separate")) ram_3 (
    .addr(aluResult_MEM[7:2]), .din(wdata2), .data(rdata2), .str(weMEM_ctrl_uMEM_MEM), .sel(byteSel[2]),
    .clk(clk), .ld(not_1_out), .clr(reset));
  Multiplexer #(.select(2), .width(8), .disabled(0), .enable("false")) multiplexer_4 (
    .in0(rdata0), .in1(rdata1), .in2(rdata2), .in3(rdata3), .out(multiplexer_4_out), .sel(aluResult_MEM[1:0]));
  assign bit_extender_1_out = {{24{1'b0}}, multiplexer_4_out};  // Bit_Extender bit_extender_1
  assign bit_extender_2_out = {{24{multiplexer_4_out[7]}}, multiplexer_4_out};  // Bit_Extender bit_extender_2
  Multiplexer #(.width(16), .disabled(0), .enable("false")) multiplexer_5 (
    .in0({rdata1, rdata0}), .in1({rdata3, rdata2}), .out(multiplexer_5_out), .sel(aluResult_MEM[1]));
  // Probe on rdata3
  RAM #(.addrWidth(6), .bus("separate")) ram_4 (
    .addr(aluResult_MEM[7:2]), .din(wdata3), .data(rdata3), .str(weMEM_ctrl_uMEM_MEM), .sel(byteSel[3]),
    .clk(clk), .ld(not_1_out), .clr(reset));
  Multiplexer #(.width(32), .disabled(0), .enable("false")) multiplexer_6 (
    .in0(bit_extender_1_out), .in1(bit_extender_2_out), .out(readByteData), .sel(memReadDataExt_ctrl_uMEM_MEM));
  assign bit_extender_3_out = {{16{1'b0}}, multiplexer_5_out};  // Bit_Extender bit_extender_3
  assign bit_extender_4_out = {{16{multiplexer_5_out[15]}}, multiplexer_5_out};  // Bit_Extender bit_extender_4
  Multiplexer #(.width(32), .disabled(0), .enable("false")) multiplexer_7 (
    .in0(bit_extender_3_out), .in1(bit_extender_4_out), .out(readHalfWordData),
    .sel(memReadDataExt_ctrl_uMEM_MEM));
  Multiplexer #(.width(32), .disabled(0), .enable("false")) multiplexer_8 (
    .in0(aluResult_MEM), .in1(readMemData), .out(wRegData_MEM), .sel(wRegDataSrc_ctrl_uMEM_MEM));
  Multiplexer #(.select(2), .width(32), .disabled(0), .enable("false")) multiplexer_9 (
    .in0({32{1'b0}}), .in1(readByteData), .in2(readHalfWordData), .in3({rdata3, rdata2, rdata1, rdata0}),
    .out(readMemData), .sel(wrMemByteSelScr_ctrl_uMEM_MEM));

  // Other names for the same wires on the sheet: wMemData[31:0] = wMemData_MEM;
  //   readWordData[31:0] = {rdata3, rdata2, rdata1, rdata0}; aluResult[31:0] = aluResult_MEM;
  //   byteAddr[1:0] = aluResult_MEM[1:0]; addr[5:0] = aluResult_MEM[7:2];
  //   memReadDataExt_ctrl_uMEM = memReadDataExt_ctrl_uMEM_MEM; weMEM_ctrl = weMEM_ctrl_uMEM_MEM;
  //   wRegDataSrc_ctrl = wRegDataSrc_ctrl_uMEM_MEM; wrMemByteSelScr_ctrl[1:0] = wrMemByteSelScr_ctrl_uMEM_MEM

  // Notes on the sheet:
  //   根据低位的2位地址，以及存取数据的类型生成存取器片选信号
  //   根据字节\半字\字重新生成要送到存储器写数据端口的信号
  //   根据字节/半字/字整理存储器读出的数据
  //   对读出的字节/半字进行扩展
  //   选择要传入到WB阶段的数据的来源
endmodule

module ALU (
  input  [3:0] aluop,
  input  [31:0] A,
  input  [31:0] B,
  output [31:0] aluResult
);

  wire priority_encoder_1_gs;
  wire [1:0] priority_encoder_1_out;
  wire [31:0] addResult, sraResult, srlResult;

  Priority_Encoder #(.select(2), .disabled(0)) priority_encoder_1 (
    .in0(aluop[0]), .in1(aluop[1]), .in2(aluop[2]), .in3(aluop[3]), .out(priority_encoder_1_out),
    .gs(priority_encoder_1_gs));  // open: en_out, en_in
  Adder #(.width(32)) adder_1 (.a(A), .b(B), .out(addResult), .cin(1'b0));  // open: cout
  Shifter #(.width(32), .shift("lr")) shifter_1 (.in(A), .\dist (B[4:0]), .out(srlResult));
  Shifter #(.width(32), .shift("ar")) shifter_2 (.in(A), .\dist (B[4:0]), .out(sraResult));
  Multiplexer #(.select(2), .width(32), .disabled(0)) multiplexer_1 (
    .in0({32{1'b0}}), .in1(addResult), .in2(srlResult), .in3(sraResult), .out(aluResult),
    .sel(priority_encoder_1_out), .en(priority_encoder_1_gs));
endmodule

module RegFiles (
  input  clk,
  input  rest,
  input  [4:0] raddr1_ID,
  input  [4:0] raddr2_ID,
  input  [31:0] wr_data_WB,
  input  [4:0] wr_addr_WB,
  input  wr_en_ctrl_WB,
  output [31:0] rdata1,
  output [31:0] rdata2
);

  wire and_1_out, and_2_out, comparator_1_eq, comparator_2_eq, comparator_3_eq, comparator_4_eq, not_1_out,
       not_2_out, S1, S2, S3, S4, S5, S6, S7, S8, S9, S10, S11, S12, S13, S14, S15, S16, S17, S18, S19, S20,
       S21, S22, S23, S24, S25, S26, S27, S28, S29, S30, S31;
  wire [31:0] D0, D1, D2, D3, D4, D5, D6, D7, D8, D9, D10, D11, D12, D13, D14, D15, D16, D17, D18, D19, D20,
       D21, D22, D23, D24, D25, D26, D27, D28, D29, D30, D31, multiplexer_1_out, multiplexer_2_out;

  // Probe on raddr1_ID
  Decoder #(.select(5), .disabled(0)) decoder_1 (
    .out1(S1), .out2(S2), .out3(S3), .out4(S4), .out5(S5), .out6(S6), .out7(S7), .out8(S8), .out9(S9),
    .out10(S10), .out11(S11), .out12(S12), .out13(S13), .out14(S14), .out15(S15), .out16(S16), .out17(S17),
    .out18(S18), .out19(S19), .out20(S20), .out21(S21), .out22(S22), .out23(S23), .out24(S24), .out25(S25),
    .out26(S26), .out27(S27), .out28(S28), .out29(S29), .out30(S30), .out31(S31), .sel(wr_addr_WB),
    .en(wr_en_ctrl_WB));  // open: out0
  // Probe on raddr1_ID
  Register #(.width(32)) R0 (.D(wr_data_WB), .en(1'b0), .Q(D0), .clk(clk), .clr(rest));
  Register #(.width(32)) R4 (.D(wr_data_WB), .en(S4), .Q(D4), .clk(clk), .clr(rest));
  Register #(.width(32)) R8 (.D(wr_data_WB), .en(S8), .Q(D8), .clk(clk), .clr(rest));
  Register #(.width(32)) Reg12 (.D(wr_data_WB), .en(S12), .Q(D12), .clk(clk), .clr(rest));
  Register #(.width(32)) register_1 (.D(wr_data_WB), .en(S16), .Q(D16), .clk(clk), .clr(rest));
  Register #(.width(32)) register_2 (.D(wr_data_WB), .en(S20), .Q(D20), .clk(clk), .clr(rest));
  Register #(.width(32)) register_3 (.D(wr_data_WB), .en(S24), .Q(D24), .clk(clk), .clr(rest));
  Register #(.width(32)) register_4 (.D(wr_data_WB), .en(S28), .Q(D28), .clk(clk), .clr(rest));
  Register #(.width(32)) R1 (.D(wr_data_WB), .en(S1), .Q(D1), .clk(clk), .clr(rest));
  Register #(.width(32)) R5 (.D(wr_data_WB), .en(S5), .Q(D5), .clk(clk), .clr(rest));
  Register #(.width(32)) R9 (.D(wr_data_WB), .en(S9), .Q(D9), .clk(clk), .clr(rest));
  Register #(.width(32)) Reg13 (.D(wr_data_WB), .en(S13), .Q(D13), .clk(clk), .clr(rest));
  Register #(.width(32)) register_5 (.D(wr_data_WB), .en(S17), .Q(D17), .clk(clk), .clr(rest));
  Register #(.width(32)) register_6 (.D(wr_data_WB), .en(S21), .Q(D21), .clk(clk), .clr(rest));
  Register #(.width(32)) register_7 (.D(wr_data_WB), .en(S25), .Q(D25), .clk(clk), .clr(rest));
  Register #(.width(32)) register_8 (.D(wr_data_WB), .en(S29), .Q(D29), .clk(clk), .clr(rest));
  Register #(.width(32)) R2 (.D(wr_data_WB), .en(S2), .Q(D2), .clk(clk), .clr(rest));
  Register #(.width(32)) R6 (.D(wr_data_WB), .en(S6), .Q(D6), .clk(clk), .clr(rest));
  Register #(.width(32)) R10 (.D(wr_data_WB), .en(S10), .Q(D10), .clk(clk), .clr(rest));
  Register #(.width(32)) Reg14 (.D(wr_data_WB), .en(S14), .Q(D14), .clk(clk), .clr(rest));
  Register #(.width(32)) register_9 (.D(wr_data_WB), .en(S18), .Q(D18), .clk(clk), .clr(rest));
  Register #(.width(32)) register_10 (.D(wr_data_WB), .en(S22), .Q(D22), .clk(clk), .clr(rest));
  Register #(.width(32)) register_11 (.D(wr_data_WB), .en(S26), .Q(D26), .clk(clk), .clr(rest));
  Register #(.width(32)) register_12 (.D(wr_data_WB), .en(S30), .Q(D30), .clk(clk), .clr(rest));
  Register #(.width(32)) R3 (.D(wr_data_WB), .en(S3), .Q(D3), .clk(clk), .clr(rest));
  Register #(.width(32)) R7 (.D(wr_data_WB), .en(S7), .Q(D7), .clk(clk), .clr(rest));
  Register #(.width(32)) R11 (.D(wr_data_WB), .en(S11), .Q(D11), .clk(clk), .clr(rest));
  Register #(.width(32)) Reg15 (.D(wr_data_WB), .en(S15), .Q(D15), .clk(clk), .clr(rest));
  Register #(.width(32)) register_13 (.D(wr_data_WB), .en(S19), .Q(D19), .clk(clk), .clr(rest));
  Register #(.width(32)) register_14 (.D(wr_data_WB), .en(S23), .Q(D23), .clk(clk), .clr(rest));
  Register #(.width(32)) register_15 (.D(wr_data_WB), .en(S27), .Q(D27), .clk(clk), .clr(rest));
  Register #(.width(32)) register_16 (.D(wr_data_WB), .en(S31), .Q(D31), .clk(clk), .clr(rest));
  Multiplexer #(.select(5), .width(32), .enable("false")) multiplexer_1 (
    .in0(D0), .in1(D1), .in2(D2), .in3(D3), .in4(D4), .in5(D5), .in6(D6), .in7(D7), .in8(D8), .in9(D9),
    .in10(D10), .in11(D11), .in12(D12), .in13(D13), .in14(D14), .in15(D15), .in16(D16), .in17(D17),
    .in18(D18), .in19(D19), .in20(D20), .in21(D21), .in22(D22), .in23(D23), .in24(D24), .in25(D25),
    .in26(D26), .in27(D27), .in28(D28), .in29(D29), .in30(D30), .in31(D31), .out(multiplexer_1_out),
    .sel(raddr1_ID));
  Multiplexer #(.select(5), .width(32), .enable("false")) multiplexer_2 (
    .in0(D0), .in1(D1), .in2(D2), .in3(D3), .in4(D4), .in5(D5), .in6(D6), .in7(D7), .in8(D8), .in9(D9),
    .in10(D10), .in11(D11), .in12(D12), .in13(D13), .in14(D14), .in15(D15), .in16(D16), .in17(D17),
    .in18(D18), .in19(D19), .in20(D20), .in21(D21), .in22(D22), .in23(D23), .in24(D24), .in25(D25),
    .in26(D26), .in27(D27), .in28(D28), .in29(D29), .in30(D30), .in31(D31), .out(multiplexer_2_out),
    .sel(raddr2_ID));
  Comparator #(.width(5), .mode("unsigned")) comparator_1 (
    .a(wr_addr_WB), .b(raddr1_ID), .eq(comparator_1_eq));  // open: gt, lt
  Comparator #(.width(5), .mode("unsigned")) comparator_2 (
    .a(raddr1_ID), .b({5{1'b0}}), .eq(comparator_2_eq));  // open: gt, lt
  Comparator #(.width(5), .mode("unsigned")) comparator_3 (
    .a(wr_addr_WB), .b(raddr2_ID), .eq(comparator_3_eq));  // open: gt, lt
  and and_1 (and_1_out, comparator_3_eq, wr_en_ctrl_WB);
  Comparator #(.width(5), .mode("unsigned")) comparator_4 (
    .a(raddr2_ID), .b({5{1'b0}}), .eq(comparator_4_eq));  // open: gt, lt
  Multiplexer #(.width(32), .disabled(0)) multiplexer_3 (
    .in0(multiplexer_1_out), .in1(wr_data_WB), .out(rdata1), .sel(and_2_out), .en(not_1_out));
  and and_2 (and_2_out, comparator_1_eq, wr_en_ctrl_WB);
  not not_1 (not_1_out, comparator_2_eq);
  Multiplexer #(.width(32), .disabled(0)) multiplexer_4 (
    .in0(multiplexer_2_out), .in1(wr_data_WB), .out(rdata2), .sel(and_1_out), .en(not_2_out));
  not not_2 (not_2_out, comparator_4_eq);

  // Other names for the same wires on the sheet: raddr1[4:0] = raddr1_ID; raddr2[4:0] = raddr2_ID
endmodule

module MEM_WB (
  input  clk,
  input  reset,
  input  flushStageWB,
  input  stallStageWB,
  input  [31:0] wRegData_MEM,
  input  [4:0] wRegAddr_MEM,
  input  weReg_ctrl_uWB_MEM,
  output [31:0] wRegData_WB,
  output [4:0] wRegAddr_WB,
  output weReg_ctrl_uWB_WB
);

  wire stall;

  not not_1 (stall, stallStageWB);
  Reg32 wRegData (.D(wRegData_MEM), .EN(stall), .flush(flushStageWB), .clk(clk), .rest(reset), .Q(wRegData_WB));
  Reg5 wRegAddr (.D(wRegAddr_MEM), .EN(stall), .flush(flushStageWB), .clk(clk), .rest(reset), .Q(wRegAddr_WB));
  Reg1 weReg_ctrl_uWB (
    .D(weReg_ctrl_uWB_MEM), .EN(stall), .flush(flushStageWB), .clk(clk), .rest(reset), .Q(weReg_ctrl_uWB_WB));

  // Other names for the same wires on the sheet: flush = flushStageWB
endmodule

module Reg32 (
  input  [31:0] D,
  input  EN,
  input  flush,
  input  clk,
  input  rest,
  output [31:0] Q
);

  wire [31:0] multiplexer_1_out;

  Multiplexer #(.width(32), .disabled(0), .enable("false")) multiplexer_1 (
    .in0(D), .in1({32{1'b0}}), .out(multiplexer_1_out), .sel(flush));
  Register #(.width(32)) register_1 (.D(multiplexer_1_out), .en(EN), .Q(Q), .clk(clk), .clr(rest));
endmodule

module Reg1 (
  input  D,
  input  EN,
  input  flush,
  input  clk,
  input  rest,
  output Q
);

  wire multiplexer_1_out;

  Multiplexer #(.disabled(0), .enable("false")) multiplexer_1 (
    .in0(D), .in1(1'b0), .out(multiplexer_1_out), .sel(flush));
  Register #(.width(1)) register_1 (.D(multiplexer_1_out), .en(EN), .Q(Q), .clk(clk), .clr(rest));
endmodule

module Reg5 (
  input  [4:0] D,
  input  EN,
  input  flush,
  input  clk,
  input  rest,
  output [4:0] Q
);

  wire [4:0] multiplexer_1_out;

  Multiplexer #(.width(5), .disabled(0), .enable("false")) multiplexer_1 (
    .in0(D), .in1({5{1'b0}}), .out(multiplexer_1_out), .sel(flush));
  Register #(.width(5)) register_1 (.D(multiplexer_1_out), .en(EN), .Q(Q), .clk(clk), .clr(rest));
endmodule

module ID_EXE (
  input  clk,
  input  reset,
  input  flushStageEXE,
  input  stallStageEXE,
  input  [3:0] aluOP_ctrl_uEXE_ID,
  input  [31:0] data1_ID,
  input  [31:0] data2_ID,
  input  [4:0] wRegAddr_ID,
  input  [31:0] wMemData_ID,
  input  weMEM_ctrl_uMEM_ID,
  input  wRegDataSrc_ctrl_uMEM_ID,
  input  [1:0] wrMemByteSelScr_ctrl_uMEM_ID,
  input  memReadDataExt_ctrl_uMEM_ID,
  input  weReg_ctrl_uWB_ID,
  output [3:0] aluOP_ctrl_uEXE_EXE,
  output [31:0] data1_EXE,
  output [31:0] data2_EXE,
  output [4:0] wRegAddr_EXE,
  output [31:0] wMemData_EXE,
  output weMEM_ctrl_uMEM_EXE,
  output wRegDataSrc_ctrl_uMEM_EXE,
  output [1:0] wrMemByteSelScr_ctrl_uMEM_EXE,
  output memReadDataExt_ctrl_uMEM_EXE,
  output weReg_ctrl_uWB_EXE
);

  wire stall;

  not not_1 (stall, stallStageEXE);
  Reg4 aluOP_ctrl_uEXE (
    .D(aluOP_ctrl_uEXE_ID), .EN(stall), .flush(flushStageEXE), .clk(clk), .rest(reset),
    .Q(aluOP_ctrl_uEXE_EXE));
  Reg32 data1 (.D(data1_ID), .EN(stall), .flush(flushStageEXE), .clk(clk), .rest(reset), .Q(data1_EXE));
  Reg32 data2 (.D(data2_ID), .EN(stall), .flush(flushStageEXE), .clk(clk), .rest(reset), .Q(data2_EXE));
  Reg5 wRegAddr (.D(wRegAddr_ID), .EN(stall), .flush(flushStageEXE), .clk(clk), .rest(reset), .Q(wRegAddr_EXE));
  Reg32 wMemData (.D(wMemData_ID), .EN(stall), .flush(flushStageEXE), .clk(clk), .rest(reset), .Q(wMemData_EXE));
  Reg1 weMEM_ctrl_uMEM (
    .D(weMEM_ctrl_uMEM_ID), .EN(stall), .flush(flushStageEXE), .clk(clk), .rest(reset),
    .Q(weMEM_ctrl_uMEM_EXE));
  Reg1 wRegDataSrc_ctrl_uMEM (
    .D(wRegDataSrc_ctrl_uMEM_ID), .EN(stall), .flush(flushStageEXE), .clk(clk), .rest(reset),
    .Q(wRegDataSrc_ctrl_uMEM_EXE));
  Reg2 wrMemByteSelScr_ctrl_uMEM (
    .D(wrMemByteSelScr_ctrl_uMEM_ID), .EN(stall), .flush(flushStageEXE), .clk(clk), .rest(reset),
    .Q(wrMemByteSelScr_ctrl_uMEM_EXE));
  Reg1 wrMemByteSelScr_ctrl_uMEM_2 (
    .D(memReadDataExt_ctrl_uMEM_ID), .EN(stall), .flush(flushStageEXE), .clk(clk), .rest(reset),
    .Q(memReadDataExt_ctrl_uMEM_EXE));
  Reg1 weReg_ctrl_uWB (
    .D(weReg_ctrl_uWB_ID), .EN(stall), .flush(flushStageEXE), .clk(clk), .rest(reset), .Q(weReg_ctrl_uWB_EXE));

  // Other names for the same wires on the sheet: flush = flushStageEXE
endmodule

module Reg4 (
  input  [3:0] D,
  input  EN,
  input  flush,
  input  clk,
  input  rest,
  output [3:0] Q
);

  wire [3:0] multiplexer_1_out;

  Multiplexer #(.width(4), .disabled(0), .enable("false")) multiplexer_1 (
    .in0(D), .in1(4'b0000), .out(multiplexer_1_out), .sel(flush));
  Register #(.width(4)) register_1 (.D(multiplexer_1_out), .en(EN), .Q(Q), .clk(clk), .clr(rest));
endmodule

module Reg3 (
  input  [2:0] D,
  input  EN,
  input  flush,
  input  clk,
  input  rest,
  output [2:0] Q
);

  wire [2:0] multiplexer_1_out;

  Multiplexer #(.width(3), .disabled(0), .enable("false")) multiplexer_1 (
    .in0(D), .in1(3'b000), .out(multiplexer_1_out), .sel(flush));
  Register #(.width(3)) register_1 (.D(multiplexer_1_out), .en(EN), .Q(Q), .clk(clk), .clr(rest));
endmodule

module Reg2 (
  input  [1:0] D,
  input  EN,
  input  flush,
  input  clk,
  input  rest,
  output [1:0] Q
);

  wire [1:0] multiplexer_1_out;

  Multiplexer #(.width(2), .disabled(0), .enable("false")) multiplexer_1 (
    .in0(D), .in1(2'b00), .out(multiplexer_1_out), .sel(flush));
  Register #(.width(2)) register_1 (.D(multiplexer_1_out), .en(EN), .Q(Q), .clk(clk), .clr(rest));
endmodule

module myCPU (
  input  clk,
  input  reset
);

  wire EXE_MEM_memreaddataext_ctrl_umem_mem, EXE_MEM_wemem_ctrl_umem_mem, EXE_MEM_wereg_ctrl_uwb_mem,
       EXE_MEM_wregdatasrc_ctrl_umem_mem, ID_branchflag_id, ID_EXE_memreaddataext_ctrl_umem_exe,
       ID_EXE_wemem_ctrl_umem_exe, ID_EXE_wereg_ctrl_uwb_exe, ID_EXE_wregdatasrc_ctrl_umem_exe,
       ID_flushreqofid_id, ID_memreaddataext_ctrl_umem_id, ID_stallreqofid_id, ID_wemem_ctrl_umem_id,
       ID_wereg_ctrl_uwb_id, ID_wregdatasrc_ctrl_umem_id, MEM_WB_wereg_ctrl_uwb_wb, plc_1_flushstageexe,
       plc_1_flushstageid, plc_1_flushstagemem, plc_1_flushstagewb, plc_1_stallstageexe, plc_1_stallstageid,
       plc_1_stallstageif, plc_1_stallstagemem, plc_1_stallstagewb;
  wire [1:0] EXE_MEM_wrmembyteselscr_ctrl_umem_mem, ID_EXE_wrmembyteselscr_ctrl_umem_exe,
       ID_wrmembyteselscr_ctrl_umem_id;
  wire [3:0] ID_aluop_ctrl_uexe_id, ID_EXE_aluop_ctrl_uexe_exe;
  wire [4:0] EXE_MEM_wregaddr_mem, ID_EXE_wregaddr_exe, ID_wregaddr_id, MEM_WB_wregaddr_wb;
  wire [31:0] ALU_aluresult_exe, EXE_MEM_aluresult_mem, EXE_MEM_wmemdata_mem, ID_branchtarget_id,
       ID_data1_id, ID_data2_id, ID_EXE_data1_exe, ID_EXE_data2_exe, ID_EXE_wmemdata_exe, ID_wmemdata_id,
       IF_ID_instr_id, IF_ID_pc_id, IF_instr_if, IF_pc_if, MEM_WB_wregdata_wb, MEM_wregdata_mem;

  // Probe on ID_branchtarget_id
  // Probe on IF_pc_if
  // Probe on IF_instr_if
  IF IF (
    .clk(clk), .rest(reset), .stallStageIF(plc_1_stallstageif), .branchTarget_ID(ID_branchtarget_id),
    .branchFlag_ID(ID_branchflag_id), .PC_IF(IF_pc_if), .instr_IF(IF_instr_if));
  // Probe on IF_ID_pc_id
  // Probe on IF_ID_instr_id
  IF_ID IF_ID (
    .clk(clk), .reset(reset), .flushStageID(plc_1_flushstageid), .stallStageID(plc_1_stallstageid),
    .PC_IF(IF_pc_if), .instr_IF(IF_instr_if), .PC_ID(IF_ID_pc_id), .instr_ID(IF_ID_instr_id));
  // Probe on ID_wregaddr_id
  // Probe on ID_wmemdata_id
  // Probe on ID_branchtarget_id
  // Probe on ID_branchflag_id
  ID ID (
    .clk(clk), .rst(reset), .PC_ID(IF_ID_pc_id), .instr_ID(IF_ID_instr_id), .wRegAddr_WB(MEM_WB_wregaddr_wb),
    .wRegData_WB(MEM_WB_wregdata_wb), .weReg_ctrl_WB(MEM_WB_wereg_ctrl_uwb_wb),
    .wRegAddr_EXE(ID_EXE_wregaddr_exe), .wRegAddr_MEM(EXE_MEM_wregaddr_mem),
    .aluResult_EXE(ALU_aluresult_exe), .wRegDataSrc_ctrl_uMEM_EXE(ID_EXE_wregdatasrc_ctrl_umem_exe),
    .wRegData_MEM(MEM_wregdata_mem), .weReg_ctrl_uWB_ID(ID_wereg_ctrl_uwb_id),
    .memReadDataExt_ctrl_uMEM_ID(ID_memreaddataext_ctrl_umem_id),
    .wrMemByteSelScr_ctrl_uMEM_ID(ID_wrmembyteselscr_ctrl_umem_id),
    .wRegDataSrc_ctrl_uMEM_ID(ID_wregdatasrc_ctrl_umem_id), .weMEM_ctrl_uMEM_ID(ID_wemem_ctrl_umem_id),
    .aluOP_ctrl_uEXE_ID(ID_aluop_ctrl_uexe_id), .data1_ID(ID_data1_id), .data2_ID(ID_data2_id),
    .wRegAddr_ID(ID_wregaddr_id), .wMemData_ID(ID_wmemdata_id), .branchTarget_ID(ID_branchtarget_id),
    .branchFlag_ID(ID_branchflag_id), .stallReqOfID_ID(ID_stallreqofid_id),
    .flushReqOfID_ID(ID_flushreqofid_id));
  PLC plc_1 (
    .stallReqOfID_ID(ID_stallreqofid_id), .flushReqOfID_ID(ID_flushreqofid_id),
    .stallStageIF(plc_1_stallstageif), .flushStageID(plc_1_flushstageid), .stallStageID(plc_1_stallstageid),
    .stallStageEXE(plc_1_stallstageexe), .flushStageEXE(plc_1_flushstageexe),
    .flushStageMEM(plc_1_flushstagemem), .stallStageMEM(plc_1_stallstagemem),
    .flushStageWB(plc_1_flushstagewb), .stallStageWB(plc_1_stallstagewb));
  // Probe on ID_data1_id
  // Probe on ID_data2_id
  // Probe on ID_aluop_ctrl_uexe_id
  // Probe on ID_EXE_wregaddr_exe
  // Probe on ID_EXE_wmemdata_exe
  // Probe on ID_EXE_wemem_ctrl_umem_exe
  // Probe on ID_EXE_wregdatasrc_ctrl_umem_exe
  // Probe on ID_EXE_wereg_ctrl_uwb_exe
  ID_EXE ID_EXE (
    .clk(clk), .reset(reset), .flushStageEXE(plc_1_flushstageexe), .stallStageEXE(plc_1_stallstageexe),
    .aluOP_ctrl_uEXE_ID(ID_aluop_ctrl_uexe_id), .data1_ID(ID_data1_id), .data2_ID(ID_data2_id),
    .wRegAddr_ID(ID_wregaddr_id), .wMemData_ID(ID_wmemdata_id), .weMEM_ctrl_uMEM_ID(ID_wemem_ctrl_umem_id),
    .wRegDataSrc_ctrl_uMEM_ID(ID_wregdatasrc_ctrl_umem_id),
    .wrMemByteSelScr_ctrl_uMEM_ID(ID_wrmembyteselscr_ctrl_umem_id),
    .memReadDataExt_ctrl_uMEM_ID(ID_memreaddataext_ctrl_umem_id), .weReg_ctrl_uWB_ID(ID_wereg_ctrl_uwb_id),
    .aluOP_ctrl_uEXE_EXE(ID_EXE_aluop_ctrl_uexe_exe), .data1_EXE(ID_EXE_data1_exe),
    .data2_EXE(ID_EXE_data2_exe), .wRegAddr_EXE(ID_EXE_wregaddr_exe), .wMemData_EXE(ID_EXE_wmemdata_exe),
    .weMEM_ctrl_uMEM_EXE(ID_EXE_wemem_ctrl_umem_exe),
    .wRegDataSrc_ctrl_uMEM_EXE(ID_EXE_wregdatasrc_ctrl_umem_exe),
    .wrMemByteSelScr_ctrl_uMEM_EXE(ID_EXE_wrmembyteselscr_ctrl_umem_exe),
    .memReadDataExt_ctrl_uMEM_EXE(ID_EXE_memreaddataext_ctrl_umem_exe),
    .weReg_ctrl_uWB_EXE(ID_EXE_wereg_ctrl_uwb_exe));
  EXE ALU (
    .aluOP_ctrl_uEXE_EXE(ID_EXE_aluop_ctrl_uexe_exe), .data1_EXE(ID_EXE_data1_exe),
    .data2_EXE(ID_EXE_data2_exe), .aluResult_EXE(ALU_aluresult_exe));
  // Probe on ALU_aluresult_exe
  // Probe on EXE_MEM_wereg_ctrl_uwb_mem
  // Probe on EXE_MEM_wregdatasrc_ctrl_umem_mem
  // Probe on EXE_MEM_aluresult_mem
  EXE_MEM EXE_MEM (
    .clk(clk), .reset(reset), .flushStageMEM(plc_1_flushstagemem), .stallStageMEM(plc_1_stallstagemem),
    .aluResult_EXE(ALU_aluresult_exe), .wRegAddr_EXE(ID_EXE_wregaddr_exe),
    .wMemData_EXE(ID_EXE_wmemdata_exe), .weMem_ctrl_uMEM_EXE(ID_EXE_wemem_ctrl_umem_exe),
    .wRegDataSrc_ctrl_uMEM_EXE(ID_EXE_wregdatasrc_ctrl_umem_exe),
    .wrMemByteSelScr_ctrl_uMEM_EXE(ID_EXE_wrmembyteselscr_ctrl_umem_exe),
    .memReadDataExt_ctrl_uMEM_EXE(ID_EXE_memreaddataext_ctrl_umem_exe),
    .weReg_ctrl_uWB_EXE(ID_EXE_wereg_ctrl_uwb_exe), .aluResult_MEM(EXE_MEM_aluresult_mem),
    .wRegAddr_MEM(EXE_MEM_wregaddr_mem), .wMemData_MEM(EXE_MEM_wmemdata_mem),
    .weMem_ctrl_uMEM_MEM(EXE_MEM_wemem_ctrl_umem_mem),
    .wRegDataSrc_ctrl_uMEM_MEM(EXE_MEM_wregdatasrc_ctrl_umem_mem),
    .wrMemByteSelScr_ctrl_uMEM_MEM(EXE_MEM_wrmembyteselscr_ctrl_umem_mem),
    .memReadDataExt_ctrl_uMEM_MEM(EXE_MEM_memreaddataext_ctrl_umem_mem),
    .weReg_ctrl_uWB_MEM(EXE_MEM_wereg_ctrl_uwb_mem));
  // Probe on EXE_MEM_wregaddr_mem
  // Probe on EXE_MEM_wmemdata_mem
  // Probe on EXE_MEM_wemem_ctrl_umem_mem
  // Probe on MEM_wregdata_mem
  MEM MEM (
    .clk(clk), .reset(reset), .aluResult_MEM(EXE_MEM_aluresult_mem), .wMemData_MEM(EXE_MEM_wmemdata_mem),
    .weMEM_ctrl_uMEM_MEM(EXE_MEM_wemem_ctrl_umem_mem),
    .wRegDataSrc_ctrl_uMEM_MEM(EXE_MEM_wregdatasrc_ctrl_umem_mem),
    .wrMemByteSelScr_ctrl_uMEM_MEM(EXE_MEM_wrmembyteselscr_ctrl_umem_mem),
    .memReadDataExt_ctrl_uMEM_MEM(EXE_MEM_memreaddataext_ctrl_umem_mem), .wRegData_MEM(MEM_wregdata_mem));
  // Probe on MEM_WB_wregdata_wb
  // Probe on MEM_WB_wregaddr_wb
  // Probe on MEM_WB_wereg_ctrl_uwb_wb
  MEM_WB MEM_WB (
    .clk(clk), .reset(reset), .flushStageWB(plc_1_flushstagewb), .stallStageWB(plc_1_stallstagewb),
    .wRegData_MEM(MEM_wregdata_mem), .wRegAddr_MEM(EXE_MEM_wregaddr_mem),
    .weReg_ctrl_uWB_MEM(EXE_MEM_wereg_ctrl_uwb_mem), .wRegData_WB(MEM_WB_wregdata_wb),
    .wRegAddr_WB(MEM_WB_wregaddr_wb), .weReg_ctrl_uWB_WB(MEM_WB_wereg_ctrl_uwb_wb));
endmodule

module PLC (
  input  stallReqOfID_ID,
  input  flushReqOfID_ID,
  output stallStageWB,
  output flushStageWB,
  output stallStageID,
  output stallStageMEM,
  output flushStageMEM,
  output flushStageID,
  output flushStageEXE,
  output stallStageIF,
  output stallStageEXE
);

  wire not_1_out, not_2_out;

  not not_1 (not_1_out, stallReqOfID_ID);
  not not_2 (not_2_out, flushReqOfID_ID);
  and and_1 (flushStageID, not_1_out, flushReqOfID_ID);

  assign flushStageEXE = stallReqOfID_ID;
  assign flushStageMEM = 1'b0;
  assign flushStageWB = 1'b0;
  assign stallStageEXE = 1'b0;
  assign stallStageID = stallReqOfID_ID;
  assign stallStageIF = stallReqOfID_ID;
  assign stallStageMEM = 1'b0;
  assign stallStageWB = 1'b0;
endmodule
